# Fritzing sketch Sketch (saved by Fritzing 1.0.1rc)
breadboards: 1

parts:
  Part1 = Arduino Nano (Rev3.0)
  HC-SR04_Sensor_1 = HC-SR04 Ultrasonic Distance Sensor
  LED1 = LED - 3mm [color="Green (565nm)" current=0.030 package="3 mm [THT]"]
  R1 = Resistor [tolerance=±5% power=0.25 resistance=330 package=THT]
  R2 = Resistor [tolerance=±5% power=0.25 resistance=330 package=THT]
  LED2 = LED - 3mm [color="Red (660nm)" current=0.030 package="3 mm [THT]"]
  LED3 = LED - 3mm [color="White (4500K)" current=0.030 package="3 mm [THT]"]
  R3 = Resistor [tolerance=±5% power=0.25 resistance=330 package=THT]
  S1 = Pushbutton [package="[THT]"]
  Part2 = ws2812b [package="smd 2812b"]

nets:
  GND: Part1.GND, HC-SR04_Sensor_1.GND, LED1.cathode, LED2.cathode, LED3.cathode, S1.Pin_1, S1.Pin_2, Part2.VSS
  N1: Part1.D4, HC-SR04_Sensor_1.TRIG
  N2: Part1.D5, HC-SR04_Sensor_1.ECHO
  N3: Part1.D8, R2.Pin_0
  N4: Part1.D9, S1.Pin_3, S1.Pin_4
  N5: Part1.D10, R1.Pin_0
  N6: Part1.D11/MOSI, R3.Pin_0
  N7: Part1.D12/MISO, Part2.DIN
  5V: Part1.5V, HC-SR04_Sensor_1.VCC, Part2.VDD
  N8: LED1.anode, R2.Pin_1
  N9: R1.Pin_1, LED2.anode
  N10: LED3.anode, R3.Pin_1
